# Fritzing sketch asli_oyku_fritzing (saved by Fritzing 1.0.3b)
breadboards: 1

parts:
  Sensor1 = TTP223B Capacitive Touch Sensor Module
  U1 = ESP32S-HiLetgo [part_number=ESP32S-HiLetgo]
  Parça1 = RFID-RC522-v2
  LED1 = RGB LED (com. cathode, rbg) [color="Red (633nm)" current=0.030A package="5 mm [THT]"]

nets:
  GND: Sensor1.GND, U1.GND, Parça1.GND, LED1.common_cathode
  VCC: Sensor1.VCC, U1.VIN, Parça1.3.3V
  N1: Sensor1.SIG, U1.GPIO32
  N2: U1.GPIO25, LED1.red_anode
  N3: U1.GPIO26, LED1.blue_anode
  N4: U1.GPIO27, LED1.green_anode
  N5: U1.GPIO5, Parça1.SDA
  N6: U1.GPIO18, Parça1.SCK
  N7: U1.GPIO19, Parça1.MISO
  N8: U1.GPIO21, Parça1.RST
  N9: U1.GPIO23, Parça1.MOSI

custom parts:
  TTP223B Capacitive Touch Sensor Module: The TTP223B capacitive touch sensor module uses the TTP223B IC. The appropriate voltage is approximately 2 to 5.5 volts.
  ESP32S-HiLetgo: HiLetgo ESP-WROOM-32 ESP32 ESP-32S Development Board 2.4GHz Dual-Mode WiFi + Bluetooth Dual Cores Microcontroller The ESP32 integrated with Antenna switches, RF Balun, power amplifiers, low-noise amplifiers, filters, and management modules, and the entire solution occupies the least area of PCB. 2.4 GHz Wi-Fi plus Bluetooth dual-mode chip, with TSMC Ultra-low power consumption 40nm technology,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
  RFID-RC522-v2: A simple China made RFID-RC522 Reader; do check the pin labels, as this is a MFRC522 based clone.
